// Logisim project computer.circ as structural Verilog: 6 circuits, main circuit main
module main (
  input  in_1,
  output out_2,
  output out_3,
  output out_4,
  output [2:0] out_5,
  output [15:0] out_6,
  output [15:0] out_7,
  output [2:0] W,
  output [2:0] A,
  output [3:0] op,
  output [2:0] B,
  output [2:0] rs1,
  output [2:0] rs2,
  output [2:0] imm,
  output [2:0] imm2,
  output [15:0] out_16
);

  wire and_2_out, arithmetic_1_z, clk_out, control_1_alusrc, control_1_branch, control_1_btype,
       control_1_regwrite, control_1_stop, not_1_out;
  wire [15:0] adder_1_out, multiplexer_1_out, multiplexer_2_out, multiplexer_3_out, pc_reg_q,
       registerfile_1_readdata1, registerfile_1_readdata2;

  Clock clk (.out(clk_out));
  not not_1 (not_1_out, control_1_stop);
  and and_1 (out_2, clk_out, not_1_out);
  Register #(.width(16)) pc_reg (.D(adder_1_out), .en(1'b1), .clk(out_2), .Q(pc_reg_q), .clr(in_1));
  ROM #(.addrWidth(16), .dataWidth(16)) program_rom (.addr(pc_reg_q), .data({op, rs1, rs2, imm, imm2}));
  Adder #(.width(16)) adder_1 (.a(pc_reg_q), .b(multiplexer_1_out), .out(adder_1_out), .cin(1'b1));  // open: cout
  Multiplexer #(.width(16)) multiplexer_1 (.in0({16{1'b0}}), .in1(out_16), .out(multiplexer_1_out), .sel(and_2_out));
  InstructionSplit instructionsplit_1 (
    .BTYPE(control_1_btype), .B11_9(rs1), .C8_6(rs2), .D5_3(imm), .E2_0(imm2), .WRITE(W), .READ_A(A),
    .READ_B(B), .SIGN_EXT_IMM(out_16));
  Control control_1 (
    .opcode(op), .Branch(control_1_branch), .ALUSrc(control_1_alusrc), .MemRead(out_4), .MemWrite(out_3),
    .RegWrite(control_1_regwrite), .BType(control_1_btype), .ALUOp(out_5), .Stop(control_1_stop));
  and and_2 (and_2_out, arithmetic_1_z, control_1_branch);
  RegisterFile registerfile_1 (
    .clk(out_2), .writeenable(control_1_regwrite), .writereg(W), .readreg1(A), .readreg2(B),
    .writedata(multiplexer_3_out), .readdata1(registerfile_1_readdata1), .readdata2(registerfile_1_readdata2));
  Multiplexer #(.width(16)) multiplexer_2 (
    .in0(registerfile_1_readdata2), .in1(out_16), .out(multiplexer_2_out), .sel(control_1_alusrc));
  Multiplexer #(.width(16)) multiplexer_3 (.in0(out_6), .in1(out_7), .out(multiplexer_3_out), .sel(out_4));
  Arithmetic arithmetic_1 (
    .o(out_5), .a(registerfile_1_readdata1), .b(multiplexer_2_out), .r(out_6), .z(arithmetic_1_z));
  RAM #(.addrWidth(16), .dataWidth(16), .trigger("falling")) ram_1 (
    .addr(out_6), .we(out_3), .oe(out_4), .clk(out_2), .din(registerfile_1_readdata2), .dout(out_7));
  Clock clock_1 ();  // open: out
  RAM #(.addrWidth(16), .dataWidth(16)) ram_2 ();  // open: addr, we, oe, clk, din, dout

  // Notes on the sheet:
  //   contents of program_rom (hex, n*v repeats v):
  //   7400 7200 760a 488 7241 9641 903c 8414 a000
  //   ram needs to be falling edge?
endmodule

module Control (
  input  [3:0] opcode,
  output Branch,
  output ALUSrc,
  output MemRead,
  output MemWrite,
  output RegWrite,
  output BType,
  output [2:0] ALUOp,
  output Stop
);

  wire and_1_out, and_3_out, nand_1_out, not_1_out, not_2_out, not_3_out, not_4_out, not_5_out, not_6_out,
       not_7_out, not_8_out, not_9_out;

  and and_1 (and_1_out, opcode[2], opcode[1]);
  not not_1 (not_1_out, opcode[0]);
  not not_2 (not_2_out, opcode[1]);
  not not_3 (not_3_out, opcode[2]);
  not not_4 (not_4_out, opcode[0]);
  not not_5 (not_5_out, opcode[0]);
  not not_6 (not_6_out, opcode[1]);
  not not_7 (not_7_out, opcode[2]);
  not not_8 (not_8_out, opcode[2]);
  not not_9 (not_9_out, opcode[0]);
  and and_2 (Branch, opcode[0], opcode[3]);
  or or_1 (ALUSrc, and_1_out, and_3_out);
  and and_3 (and_3_out, not_1_out, not_2_out, not_3_out, opcode[3]);
  and and_4 (MemRead, opcode[2], opcode[1], not_4_out);
  and and_5 (MemWrite, opcode[3], not_5_out);
  not not_10 (RegWrite, opcode[3]);
  and and_6 (ALUOp[2], opcode[2], not_6_out);
  and and_7 (ALUOp[1], not_7_out, opcode[1]);
  nand nand_1 (nand_1_out, opcode[2], opcode[1]);
  and and_8 (ALUOp[0], nand_1_out, opcode[0]);
  and and_9 (Stop, opcode[3], not_8_out, opcode[1], not_9_out);

  assign BType = opcode[3];
endmodule

module RegisterFile (
  input  clk,
  input  writeenable,
  input  [2:0] writereg,
  input  [2:0] readreg1,
  input  [2:0] readreg2,
  input  [15:0] writedata,
  output [15:0] readdata1,
  output [15:0] readdata2
);

  wire and_1_out, and_2_out, and_3_out, and_4_out, and_5_out, and_6_out, and_7_out, decoder_1_out1,
       decoder_1_out2, decoder_1_out3, decoder_1_out4, decoder_1_out5, decoder_1_out6, decoder_1_out7;
  wire [15:0] register_1_q, register_2_q, register_3_q, register_4_q, register_5_q, register_6_q,
       register_7_q, register_8_q;

  Decoder #(.select(3)) decoder_1 (
    .out1(decoder_1_out1), .out2(decoder_1_out2), .out3(decoder_1_out3), .out4(decoder_1_out4),
    .out5(decoder_1_out5), .out6(decoder_1_out6), .out7(decoder_1_out7), .sel(writereg));  // open: out0, en
  Register #(.width(16)) register_1 (.D(writedata), .en(1'b0), .clk(clk), .Q(register_1_q));  // open: clr
  Register #(.width(16)) register_2 (.D(writedata), .en(and_1_out), .clk(clk), .Q(register_2_q));  // open: clr
  and and_1 (and_1_out, writeenable, decoder_1_out1);
  Register #(.width(16)) register_3 (.D(writedata), .en(and_2_out), .clk(clk), .Q(register_3_q));  // open: clr
  and and_2 (and_2_out, writeenable, decoder_1_out2);
  Register #(.width(16)) register_4 (.D(writedata), .en(and_3_out), .clk(clk), .Q(register_4_q));  // open: clr
  and and_3 (and_3_out, writeenable, decoder_1_out3);
  and and_4 (and_4_out, writeenable, decoder_1_out4);
  and and_5 (and_5_out, writeenable, decoder_1_out5);
  and and_6 (and_6_out, writeenable, decoder_1_out6);
  and and_7 (and_7_out, writeenable, decoder_1_out7);
  Register #(.width(16)) register_5 (.D(writedata), .en(and_4_out), .clk(clk), .Q(register_5_q));  // open: clr
  Register #(.width(16)) register_6 (.D(writedata), .en(and_5_out), .clk(clk), .Q(register_6_q));  // open: clr
  Register #(.width(16)) register_7 (.D(writedata), .en(and_6_out), .clk(clk), .Q(register_7_q));  // open: clr
  Register #(.width(16)) register_8 (.D(writedata), .en(and_7_out), .clk(clk), .Q(register_8_q));  // open: clr
  Multiplexer #(.select(3), .width(16)) multiplexer_1 (
    .in0(register_1_q), .in1(register_2_q), .in2(register_3_q), .in3(register_4_q), .in4(register_5_q),
    .in5(register_6_q), .in6(register_7_q), .in7(register_8_q), .out(readdata1), .sel(readreg1));
  Multiplexer #(.select(3), .width(16)) multiplexer_2 (
    .in0(register_1_q), .in1(register_2_q), .in2(register_3_q), .in3(register_4_q), .in4(register_5_q),
    .in5(register_6_q), .in6(register_7_q), .in7(register_8_q), .out(readdata2), .sel(readreg2));
endmodule

module Arithmetic (
  input  [2:0] o,
  input  [15:0] a,
  input  [15:0] b,
  output [15:0] r,
  output z
);

  wire [15:0] adder_1_out, subtractor_1_out;

  Adder #(.width(16)) adder_1 (.a(a), .b(b), .out(adder_1_out));  // open: cin, cout
  Subtractor #(.width(16)) subtractor_1 (.a(a), .b(b), .out(subtractor_1_out));  // open: bin, bout
  Comparator #(.width(16)) comparator_1 (.a(subtractor_1_out), .b({16{1'b0}}), .eq(z));  // open: gt, lt
  Multiplexer #(.select(3), .width(16)) multiplexer_1 (
    .in0(adder_1_out), .in1(subtractor_1_out), .out(r), .sel(o));  // open: in2, in3, in4, in5, in6, in7
endmodule

module InstructionSplit (
  input  BTYPE,
  input  [2:0] B11_9,
  input  [2:0] C8_6,
  input  [2:0] D5_3,
  input  [2:0] E2_0,
  output [2:0] WRITE,
  output [2:0] READ_A,
  output [2:0] READ_B,
  output [15:0] SIGN_EXT_IMM
);

  Multiplexer #(.width(3)) multiplexer_1 (.in0(D5_3), .in1(B11_9), .out(READ_B), .sel(BTYPE));

  assign READ_A = C8_6;
  assign SIGN_EXT_IMM = {{11{D5_3[2]}}, D5_3[1:0], E2_0};
  assign WRITE = B11_9;

  // Notes on the sheet:
  //   rtype: op rd rs1 rs2 unused
  //   itype: op rd rs1 imm6
  //   btype: op rs2 rs1 off6
endmodule

module memtest (
  input  [7:0] in_1,
  input  [15:0] in_2,
  input  in_3,
  input  in_4,
  output [15:0] out_5
);

  wire clock_1_out;
  wire [7:0] adder_1_out, or_1_out;
  wire [15:0] ram_1_dout;

  Clock clock_1 (.out(clock_1_out));
  Adder adder_1 (.out(adder_1_out));  // open: a, b, cin, cout
  RAM #(.addrWidth(16), .dataWidth(16)) ram_1 (
    .addr(in_2), .we(in_3), .oe(in_4), .clk(clock_1_out), .dout(ram_1_dout));  // open: din
  assign or_1_out = in_1 | adder_1_out;  // OR_Gate or_1, 8 bits wide
  assign out_5 = ram_1_dout;  // OR_Gate or_2, 16 bits wide OR_Gate

  // Notes on the sheet:
  //   in_4: initial=0x1
  //   in_2: initial=0x1
endmodule
