// Logisim project computer_mod.circ as structural Verilog: 7 circuits, main circuit main
module main (
  input  in_1,
  input  in_2,
  input  in_3,
  output out_4,
  output out_5,
  output out_6,
  output [2:0] out_7,
  output [15:0] out_8,
  output [15:0] out_9,
  output [15:0] out_10,
  output [2:0] W,
  output [3:0] op,
  output [2:0] A,
  output [2:0] rs1,
  output [2:0] B,
  output [2:0] rs2,
  output [2:0] imm,
  output [2:0] imm2,
  output [15:0] out_19
);

  wire and_1_out, arithmetic_1_z, control_1_alusrc, control_1_branch, control_1_btype, control_1_regwrite;
  wire [3:0] binary_to_bcd_converter_1_p2, binary_to_bcd_converter_1_p3, binary_to_bcd_converter_1_p4;
  wire [15:0] adder_1_out, multiplexer_1_out, multiplexer_2_out, multiplexer_3_out, pc_reg_q,
       registerfile_1_r2_out, registerfile_1_readdata1;

  Register #(.width(16)) pc_reg (.D(adder_1_out), .en(1'b1), .clk(in_1), .Q(pc_reg_q), .clr(in_2));
  ROM #(.addrWidth(16), .dataWidth(16)) program_rom (.addr(pc_reg_q), .data({op, rs1, rs2, imm, imm2}));
  Adder #(.width(16)) adder_1 (.a(pc_reg_q), .b(multiplexer_1_out), .out(adder_1_out), .cin(1'b1));  // open: cout
  Multiplexer #(.width(16)) multiplexer_1 (.in0({16{1'b0}}), .in1(out_19), .out(multiplexer_1_out), .sel(and_1_out));
  InstructionSplit instructionsplit_1 (
    .BTYPE(control_1_btype), .B11_9(rs1), .C8_6(rs2), .D5_3(imm), .E2_0(imm2), .WRITE(W), .READ_A(A),
    .READ_B(B), .SIGN_EXT_IMM(out_19));
  Control control_1 (
    .opcode(op), .Branch(control_1_branch), .ALUSrc(control_1_alusrc), .MemRead(out_6), .MemWrite(out_5),
    .RegWrite(control_1_regwrite), .BType(control_1_btype), .ALUOp(out_7));
  and and_1 (and_1_out, arithmetic_1_z, control_1_branch);
  RegisterFile registerfile_1 (
    .clk(in_1), .writeenable(control_1_regwrite), .writereg(W), .readreg1(A), .readreg2(B),
    .writedata(multiplexer_3_out), .CLEAR(in_3), .readdata1(registerfile_1_readdata1), .readdata2(out_10),
    .R2_OUT(registerfile_1_r2_out));
  Multiplexer #(.width(16)) multiplexer_2 (.in0(out_10), .in1(out_19), .out(multiplexer_2_out), .sel(control_1_alusrc));
  Multiplexer #(.width(16)) multiplexer_3 (.in0(out_8), .in1(out_9), .out(multiplexer_3_out), .sel(out_6));
  Arithmetic arithmetic_1 (
    .o(out_7), .a(registerfile_1_readdata1), .b(multiplexer_2_out), .r(out_8), .Z(arithmetic_1_z));  // open: P, N
  Hex_Digit_Display hex_digit_display_1 (.value(binary_to_bcd_converter_1_p2));  // open: dp
  // Binary_to_BCD_converter #(.binvalue(8)) binary_to_bcd_converter_1: pin names not known; wires that end beside it: registerfile_1_r2_out[7:0], binary_to_bcd_converter_1_p2, binary_to_bcd_converter_1_p3, binary_to_bcd_converter_1_p4
  Hex_Digit_Display hex_digit_display_2 (.value(binary_to_bcd_converter_1_p3));  // open: dp
  Hex_Digit_Display hex_digit_display_3 (.value(binary_to_bcd_converter_1_p4));  // open: dp
  RAM #(.addrWidth(16), .dataWidth(16), .trigger("falling"), .\type ("nonvolatile")) ram_1 (
    .addr(out_8), .we(out_5), .oe(out_6), .clk(in_1), .din(out_10), .dout(out_9));
  RAM #(.addrWidth(16), .dataWidth(16)) ram_2 ();  // open: addr, we, oe, clk, din, dout

  assign out_4 = in_1;

  // Notes on the sheet:
  //   contents of program_rom (hex, n*v repeats v):
  //   7600 6401 6801 24a0 911a 6901 9e04 9e07
endmodule

module Control (
  input  [3:0] opcode,
  output Branch,
  output ALUSrc,
  output MemRead,
  output MemWrite,
  output RegWrite,
  output BType,
  output [2:0] ALUOp
);

  wire and_1_out, and_2_out, and_3_out, and_4_out, and_5_out, nand_1_out, not_1_out, not_2_out, not_3_out,
       not_4_out, not_5_out, not_6_out, not_7_out, not_8_out, not_9_out, not_10_out, or_1_out, plarom_1_p7;
  wire [2:0] and_8_out;
  wire [3:0] plarom_1_p4;

  and and_1 (and_1_out, plarom_1_p4[2], plarom_1_p4[1]);
  // NOT_Gate not_1 has open pins: in=open, out=not_1_out
  // NOT_Gate not_2 has open pins: in=open, out=not_2_out
  // NOT_Gate not_3 has open pins: in=open, out=not_3_out
  not not_4 (not_4_out, plarom_1_p4[0]);
  not not_5 (not_5_out, plarom_1_p4[0]);
  not not_6 (not_6_out, plarom_1_p4[1]);
  not not_7 (not_7_out, plarom_1_p4[2]);
  not not_8 (not_8_out, plarom_1_p4[2]);
  not not_9 (not_9_out, plarom_1_p4[0]);
  // PlaRom #(.Contents("1*7 2 1 1 2 1*3 2 2 1 2 1*3 2 1 2 1 2 2 1 1 2*4 1*3 2 1 1 2 0*4 1 0*8 1 0*3 1 0*4 1 0 0 1 0*5 1 0 0 1 1 0*4 1 0 1 0*6 1 0 1 0 1 0 1 0 0 1 0*5 1 1 0 1 0*5 1 0 1 0 1 0*3 1 0*4 1 0 0 1"), .\and (10), .outputs(9)) plarom_1: pin names not known; wires that end beside it: plarom_1_p4[3], plarom_1_p4[2], plarom_1_p4[1], plarom_1_p4[0], opcode, {Branch, ALUSrc, MemRead, MemWrite, RegWrite, BType, ALUOp}, plarom_1_p7
  and and_2 (and_2_out, plarom_1_p4[0], plarom_1_p4[3]);
  or or_1 (or_1_out, and_1_out, and_3_out);
  and and_3 (and_3_out, not_1_out, not_2_out, not_3_out, plarom_1_p4[3]);
  and and_4 (and_4_out, plarom_1_p4[2], plarom_1_p4[1], not_4_out);
  and and_5 (and_5_out, plarom_1_p4[3], not_5_out);
  not not_10 (not_10_out, plarom_1_p4[3]);
  and and_6 (and_8_out[2], plarom_1_p4[2], not_6_out);
  and and_7 (and_8_out[1], not_7_out, plarom_1_p4[1]);
  nand nand_1 (nand_1_out, plarom_1_p4[2], plarom_1_p4[1]);
  and and_8 (and_8_out[0], nand_1_out, plarom_1_p4[0]);
  and and_9 (plarom_1_p7, plarom_1_p4[3], not_8_out, plarom_1_p4[1], not_9_out);
  // PlaRom #(.Contents("1*7 2 1 1 2 1*3 2 2 1 2 1*3 2 1 2 1 2 2 1 1 2*4 1*3 2 1 1 2 0*4 1 0*8 1 0*3 1 0*4 1 0 1 0 1 0*4 1 0 1 0 1 0*4 1 1 0*7 1 1 0*4 1 0 0 1 0*5 1 1 0 1 0*5 1 0 1 0*5 1 0*4 1*3 0"), .\and (10), .outputs(9)) plarom_2: pin names not known
endmodule

module RegisterFile (
  input  clk,
  input  writeenable,
  input  [2:0] writereg,
  input  [2:0] readreg1,
  input  [2:0] readreg2,
  input  [15:0] writedata,
  input  CLEAR,
  output [15:0] readdata1,
  output [15:0] readdata2,
  output [15:0] R2_OUT
);

  wire and_1_out, and_2_out, and_3_out, and_4_out, and_5_out, and_6_out, and_7_out, decoder_1_out1,
       decoder_1_out2, decoder_1_out3, decoder_1_out4, decoder_1_out5, decoder_1_out6, decoder_1_out7;
  wire [15:0] register_1_q, register_2_q, register_4_q, register_5_q, register_6_q, register_7_q,
       register_8_q;

  Decoder #(.select(3)) decoder_1 (
    .out1(decoder_1_out1), .out2(decoder_1_out2), .out3(decoder_1_out3), .out4(decoder_1_out4),
    .out5(decoder_1_out5), .out6(decoder_1_out6), .out7(decoder_1_out7), .sel(writereg));  // open: out0, en
  Register #(.width(16)) register_1 (.D(writedata), .en(1'b0), .clk(clk), .Q(register_1_q), .clr(CLEAR));
  Register #(.width(16)) register_2 (.D(writedata), .en(and_1_out), .clk(clk), .Q(register_2_q), .clr(CLEAR));
  and and_1 (and_1_out, writeenable, decoder_1_out1);
  Register #(.width(16)) register_3 (.D(writedata), .en(and_2_out), .clk(clk), .Q(R2_OUT), .clr(CLEAR));
  and and_2 (and_2_out, writeenable, decoder_1_out2);
  Register #(.width(16)) register_4 (.D(writedata), .en(and_3_out), .clk(clk), .Q(register_4_q), .clr(CLEAR));
  and and_3 (and_3_out, writeenable, decoder_1_out3);
  and and_4 (and_4_out, writeenable, decoder_1_out4);
  and and_5 (and_5_out, writeenable, decoder_1_out5);
  and and_6 (and_6_out, writeenable, decoder_1_out6);
  and and_7 (and_7_out, writeenable, decoder_1_out7);
  Register #(.width(16)) register_5 (.D(writedata), .en(and_4_out), .clk(clk), .Q(register_5_q), .clr(CLEAR));
  Register #(.width(16)) register_6 (.D(writedata), .en(and_5_out), .clk(clk), .Q(register_6_q), .clr(CLEAR));
  Register #(.width(16)) register_7 (.D(writedata), .en(and_6_out), .clk(clk), .Q(register_7_q), .clr(CLEAR));
  Register #(.width(16)) register_8 (.D(writedata), .en(and_7_out), .clk(clk), .Q(register_8_q), .clr(CLEAR));
  Multiplexer #(.select(3), .width(16)) multiplexer_1 (
    .in0(register_1_q), .in1(register_2_q), .in2(R2_OUT), .in3(register_4_q), .in4(register_5_q),
    .in5(register_6_q), .in6(register_7_q), .in7(register_8_q), .out(readdata1), .sel(readreg1));
  Multiplexer #(.select(3), .width(16)) multiplexer_2 (
    .in0(register_1_q), .in1(register_2_q), .in2(R2_OUT), .in3(register_4_q), .in4(register_5_q),
    .in5(register_6_q), .in6(register_7_q), .in7(register_8_q), .out(readdata2), .sel(readreg2));
endmodule

module Arithmetic (
  input  [2:0] o,
  input  [15:0] a,
  input  [15:0] b,
  output [15:0] r,
  output P,
  output Z,
  output N
);

  wire [15:0] adder_1_out, and_1_out, multiplier_1_out, or_1_out, subtractor_1_out, xor_1_out;

  Adder #(.width(16)) adder_1 (.a(a), .b(b), .out(adder_1_out));  // open: cin, cout
  Subtractor #(.width(16)) subtractor_1 (.a(a), .b(b), .out(subtractor_1_out));  // open: bin, bout
  Multiplier #(.width(16)) multiplier_1 (.a(a), .b(b), .out(multiplier_1_out));  // open: cin, cout
  assign and_1_out = a & b;  // AND_Gate and_1, 16 bits wide
  assign or_1_out = a | b;  // OR_Gate or_1, 16 bits wide
  assign xor_1_out = b ^ a;  // XOR_Gate xor_1, 16 bits wide
  Multiplexer #(.select(3), .width(16)) multiplexer_1 (
    .in0(adder_1_out), .in1(subtractor_1_out), .in2(multiplier_1_out), .in3(and_1_out), .in4(or_1_out),
    .in5(xor_1_out), .out(r), .sel(o));  // open: in6, in7
  Comparator #(.width(16)) comparator_1 (.a(r), .b({16{1'b0}}), .gt(P), .eq(Z), .lt(N));
endmodule

module InstructionSplit (
  input  BTYPE,
  input  [2:0] B11_9,
  input  [2:0] C8_6,
  input  [2:0] D5_3,
  input  [2:0] E2_0,
  output [2:0] WRITE,
  output [2:0] READ_A,
  output [2:0] READ_B,
  output [15:0] SIGN_EXT_IMM
);

  Multiplexer #(.width(3)) multiplexer_1 (
    .in0(D5_3), .in1(B11_9), .out({SIGN_EXT_IMM[15], SIGN_EXT_IMM[4:3]}), .sel(BTYPE));

  assign READ_A = C8_6;
  assign READ_B = D5_3;
  assign {SIGN_EXT_IMM[14:5], SIGN_EXT_IMM[2:0]} = {{10{SIGN_EXT_IMM[15]}}, E2_0};
  assign WRITE = B11_9;

  // Notes on the sheet:
  //   rtype: op rd rs1 rs2 unused
  //   itype: op rd rs1 imm6
  //   btype: op imm6:3 rs1 rs2 imm2:0
endmodule

module memtest (
  input  [7:0] in_1,
  input  [15:0] in_2,
  input  in_3,
  input  in_4,
  output [15:0] out_5
);

  wire clock_1_out;
  wire [7:0] adder_1_out, or_1_out;
  wire [15:0] ram_1_dout;

  Clock clock_1 (.out(clock_1_out));
  Adder adder_1 (.out(adder_1_out));  // open: a, b, cin, cout
  RAM #(.addrWidth(16), .dataWidth(16)) ram_1 (
    .addr(in_2), .we(in_3), .oe(in_4), .clk(clock_1_out), .dout(ram_1_dout));  // open: din
  assign or_1_out = in_1 | adder_1_out;  // OR_Gate or_1, 8 bits wide
  assign out_5 = ram_1_dout;  // OR_Gate or_2, 16 bits wide OR_Gate

  // Notes on the sheet:
  //   in_4: initial=0x1
  //   in_2: initial=0x1
endmodule

module disptest (
  input  [15:0] in_1
);

  Hex_Digit_Display hex_digit_display_1 ();  // open: value, dp
  // Binary_to_BCD_converter #(.binvalue(8)) binary_to_bcd_converter_1: pin names not known; wires that end beside it: in_1[15:8]
  Hex_Digit_Display hex_digit_display_2 ();  // open: value, dp
  Hex_Digit_Display hex_digit_display_3 ();  // open: value, dp
  Hex_Digit_Display hex_digit_display_4 ();  // open: value, dp
  // Binary_to_BCD_converter #(.binvalue(8)) binary_to_bcd_converter_2: pin names not known; wires that end beside it: in_1[7:0]
  Hex_Digit_Display hex_digit_display_5 ();  // open: value, dp
  Hex_Digit_Display hex_digit_display_6 ();  // open: value, dp

  // Notes on the sheet:
  //   in_1: initial=0xffff
endmodule
